# Fritzing sketch application (saved by Fritzing 0.9.9b)
breadboards: 1

parts:
  U1 = lolin
  DHT1 = DHT22 Humidity and Temperature Sensor
  U2 = 2-Channel 5v Relay Shield [package=relay-2ch5v10a]
  Part1 = LCD1602-I2C

nets:
  VCC: U1.connector14, U2.VCC, Part1.VCC
  GND: U1.connector15, DHT1.NULL, U2.GND, Part1.GND
  N1: U1.connector28, DHT1.DATA
  N2: U1.connector29, U2.IN1
  N3: U1.connector32, Part1.SDA
  N4: U1.connector33, Part1.SCL
  N5: U1.connector34, DHT1.VDD

custom parts:
  2-Channel 5v Relay Shield: 2 Channel 5v Relay Shield w. 2x SPD-06VDC-SD-C
  LCD1602-I2C: A standard character display, usually with 2x16 characters. Comes in many colors with LCM1602 IIC attached.
