# Fritzing sketch controling_relay (saved by Fritzing 0.9.9b)
breadboards: 1

parts:
  U1 = 2-Channel 5v Relay Shield [package=relay-2ch5v10a]
  MH-ET_LIVE_ESP32_DEVKIT1 = MH-ET LIVE ESP32 DEVKIT 38 pins
  LED1 = smd LED [color="Red (633nm)" package="0805 [SMD]"]

nets:
  VCC: U1.VCC, MH-ET_LIVE_ESP32_DEVKIT1.5V
  N1: U1.GND, MH-ET_LIVE_ESP32_DEVKIT1.GND#64, LED1.cathode
  N2: U1.IN1, MH-ET_LIVE_ESP32_DEVKIT1.IO12
  N3: U1.K1-In, MH-ET_LIVE_ESP32_DEVKIT1.IO25
  N4: U1.K1-On, LED1.anode

custom parts:
  2-Channel 5v Relay Shield: 2 Channel 5v Relay Shield w. 2x SPD-06VDC-SD-C
  MH-ET LIVE ESP32 DEVKIT 38 pins: http://mh.nodebb.com/topic/2/mh-et-live-esp32-devkit
