# Fritzing sketch ESP32 (saved by Fritzing 0.9.9b)
breadboards: 3

parts:
  MH-ET_LIVE_ESP32_DEVKIT1 = MH-ET LIVE ESP32 DEVKIT 38 pins  # not connected
  U1 = lolin
  U2 = ESP32-38PinWide [part_number=ESP32-38PinWide]  # not connected
  LED1 = LED - 5mm [color="Red (633nm)" current=0.030 package="5 mm [THT]"]
  LED2 = LED - 5mm [color="Red (633nm)" current=0.030 package="5 mm [THT]"]
  LED3 = LED - 5mm [color="Red (633nm)" current=0.030 package="5 mm [THT]"]
  LED4 = LED - 5mm [color="Red (633nm)" current=0.030 package="5 mm [THT]"]
  LED5 = LED - 5mm [color="Red (633nm)" current=0.030 package="5 mm [THT]"]
  R1 = Resistor [tolerance=±5% power=0.25 resistance=220 package=THT]
  R2 = Resistor [tolerance=±5% power=0.25 resistance=220 package=THT]
  R3 = Resistor [tolerance=±5% power=0.25 resistance=220 package=THT]
  R4 = Resistor [tolerance=±5% power=0.25 resistance=220 package=THT]
  R5 = Resistor [tolerance=±5% power=0.25 resistance=220 package=THT]
  U3 = 2-Channel 5v Relay Shield [package=relay-2ch5v10a]  # not connected
  DHT1 = DHT22 Humidity and Temperature Sensor  # not connected

nets:
  N1: U1.connector0, R1.Pin_1, R2.Pin_1, R3.Pin_1, R4.Pin_1
  N2: U1.connector15, LED1.cathode, LED2.cathode, LED3.cathode, LED4.cathode, LED5.cathode
  N3: U1.connector32, R5.Pin_1
  N4: LED1.anode, R1.Pin_0
  N5: LED2.anode, R2.Pin_0
  N6: LED3.anode, R3.Pin_0
  N7: LED4.anode, R4.Pin_0
  N8: LED5.anode, R5.Pin_0

custom parts:
  MH-ET LIVE ESP32 DEVKIT 38 pins: http://mh.nodebb.com/topic/2/mh-et-live-esp32-devkit
  ESP32-38PinWide: Generic 38-Pin ESP32 with wide format (only access to one side of pins on a breadboard) based on Stephen Lilley's HiLetgo ESP-WROOM-32 ESP32 ESP-32S Development Board.
  2-Channel 5v Relay Shield: 2 Channel 5v Relay Shield w. 2x SPD-06VDC-SD-C
